# Fritzing sketch esp32 (saved by Fritzing 0.9.3b)
breadboards: 1

parts:
  U1 = ESP32S-HiLetgo [part_number=ESP32S-HiLetgo]
  LED1 = smd LED [color="Red (633nm)" package="1206 [SMD]"]
  R1 = Resistor [tolerance=±5% resistance=220 package="0402 [SMD]"]
  DHT1 = DHT11 Humitidy and Temperature Sensor
  J1 = Basic Servo
  hc-sr1 = hc-sr04
  Grove1 = Grove Infrared Emitter

nets:
  N1: U1.GPIO33, Grove1.TX
  N2: U1.GPIO25, hc-sr1.Trig
  N3: U1.GPIO14, DHT1.DATA
  N4: U1.GPIO12, R1.Pin_0
  GND: U1.GND, LED1.anode, DHT1.GND, J1.gnd, hc-sr1.GND, Grove1.GND
  VCC: U1.VIN, DHT1.VDD, J1.vcc, hc-sr1.VCC, Grove1.VCC
  N5: LED1.cathode, R1.Pin_1

custom parts:
  ESP32S-HiLetgo: HiLetgo ESP-WROOM-32 ESP32 ESP-32S Development Board 2.4GHz Dual-Mode WiFi + Bluetooth Dual Cores Microcontroller The ESP32 integrated with Antenna switches, RF Balun, power amplifiers, low-noise amplifiers, filters, and management modules, and the entire solution occupies the least area of PCB. 2.4 GHz Wi-Fi plus Bluetooth dual-mode chip, with TSMC Ultra-low power consumption 40nm technology,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
  DHT11 Humitidy and Temperature Sensor: DHT11 Humidity and Temperature Sensor
